# Fritzing sketch Diagrama Solar Tracker (saved by Fritzing 1.0.0rc)
circuit board: 16.9333cm x 5.64444cm
breadboards: 1

parts:
  LED_PIN_12_(Left) = LED - 5mm [color="Blue (505nm)" current=0.030A package="5 mm [THT]"]
  LED_PIN_11_(Right) = LED - 5mm [color="Blue (505nm)" current=0.030A package="5 mm [THT]"]
  LED_PIN_13_(Down) = LED - 5mm [color="Red (633nm)" current=0.030A package="5 mm [THT]"]
  LED_PIN_10_(UP) = LED - 5mm [color="Blue (525nm)" current=0.030A part_number=Led_BTN_Automatico package="5 mm [THT]"]
  R9 = Resistor [tolerance=±5% resistance=220 power=0.25W package=THT]
  R10 = Resistor [tolerance=±5% resistance=220 power=0.25W package=THT]
  R11 = Resistor [tolerance=±5% resistance=220 power=0.25W package=THT]
  R12 = Resistor [tolerance=±5% resistance=220 power=0.25W package=THT]
  R5 = Resistor [tolerance=±5% resistance=220 power=0.25W package=THT]
  R4 = Resistor [tolerance=±5% resistance=220 power=0.25W package=THT]
  R3 = Resistor [tolerance=±5% resistance=220 power=0.25W package=THT]
  R6 = Resistor [tolerance=±5% resistance=220 power=0.25W package=THT]
  Servo_Vertical = Basic Servo [part_number="HiTec HS-422"]
  LDR_2_Right_PIN_A1 = Photocell (LDR) [power=0.25W dark_resistance_@0.01lx=300kΩ light_resistance_@100lx=400Ω luminance=10lx package=THT]
  LDR_4_UP_PIN_A3 = Photocell (LDR) [power=0.25W dark_resistance_@0.01lx=300kΩ light_resistance_@100lx=400Ω luminance=10lx package=THT]
  LDR_3_Down_PIN_A2 = Photocell (LDR) [power=0.25W dark_resistance_@0.01lx=300kΩ light_resistance_@100lx=400Ω luminance=10lx package=THT]  # not connected
  LDR_1_Left_PIN_A0 = Photocell (LDR) [power=0.25W dark_resistance_@0.01lx=300kΩ light_resistance_@100lx=400Ω luminance=10lx package=THT]
  Reloj_Tiny_RTC1 = Tiny RTC
  Sensor = ACS712 Current Sensor 5A 20A 30A
  Pla_Cprincipal = Arduino Mega 2560 (Rev3)
  Servo_Horizonal = Basic Servo [part_number="HiTec HS-422"]
  SD_Card = SD Card Module
  Pantalla_OLED_I2C1 = OLED 128x64 I2C Monochrome Display
  Modulo_Carga_TP1056 = TP4056 [chip_label=TP4056 package="DIP (Dual Inline) [THT]"]
  VCC1 = 4 x AAA Battery Mount
  Foto_Celda = Solar Pannel [part_number=FotoSelda]
  10K = Resistor [tolerance=±5% resistance=10k power=0.25W package=THT]
  Bluetooth = Bluetooth HC-06u [package=THT]
  Onderdeel3 = Thumb Joystick
  Modo_Manual = Momentary Switch [package=ksa_sealed_tac_switch]
  Switch-_Encendido = Round Pushbutton
  Seguir_Al_Sol = Momentary Switch [package=ksa_sealed_tac_switch]
  Un_solo_motor = Momentary Switch [package=ksa_sealed_tac_switch]
  R13 = Resistor [tolerance=±5% power=0.25W resistance=10 package=THT]
  R14 = Resistor [tolerance=±5% power=0.25W resistance=10 package=THT]
  R15 = Resistor [tolerance=±5% power=0.25W resistance=10 package=THT]

nets (from the breadboard view):
  GND: LED_PIN_12_(Left).cathode, LED_PIN_11_(Right).cathode, LED_PIN_13_(Down).cathode, LED_PIN_10_(UP).cathode, Servo_Vertical.gnd, Sensor.GND, Pla_Cprincipal.A0, Pla_Cprincipal.A1, Pla_Cprincipal.A2, Pla_Cprincipal.A3, Servo_Horizonal.gnd, SD_Card.GND, SD_Card.+5, Bluetooth.GND
  N1: LED_PIN_12_(Left).anode, R11.Pin_1, Pla_Cprincipal.D12_PWM
  N2: LED_PIN_11_(Right).anode, R10.Pin_1, Pla_Cprincipal.D11_PWM
  N3: LED_PIN_13_(Down).anode, R12.Pin_1, Pla_Cprincipal.D13_PWM
  N4: LED_PIN_10_(UP).anode, R9.Pin_1, Pla_Cprincipal.D10_PWM
  N5: R5.Pin_0, LDR_2_Right_PIN_A1.pin_0
  VCC: R5.Pin_1, R4.Pin_1, R3.Pin_1, R6.Pin_0, Servo_Vertical.vcc, Reloj_Tiny_RTC1.VCC, Sensor.VCC, Pla_Cprincipal.5V, Pantalla_OLED_I2C1.VDD, Bluetooth.VCC
  N6: R3.Pin_0, LDR_4_UP_PIN_A3.pin_0
  N7: R6.Pin_1, LDR_1_Left_PIN_A0.pin_0
  N8: Servo_Vertical.pulse, Pla_Cprincipal.D6_PWM
  N9: LDR_2_Right_PIN_A1.pin_1, LDR_4_UP_PIN_A3.pin_1, LDR_1_Left_PIN_A0.pin_1, Modulo_Carga_TP1056.pin2, Foto_Celda.pin1, 10K.Pin_0, Onderdeel3.GND, R13.Pin_0, R14.Pin_0, R15.Pin_0
  N10: Reloj_Tiny_RTC1.SCL, Pla_Cprincipal.D21/SCL, Pantalla_OLED_I2C1.SCK
  N11: Reloj_Tiny_RTC1.SDA, Pla_Cprincipal.D20/SDA, Pantalla_OLED_I2C1.SDA
  GND_2: Reloj_Tiny_RTC1.GND, Pla_Cprincipal.GND, Pantalla_OLED_I2C1.GND, Modulo_Carga_TP1056.pin6
  N12: Sensor.1, Modulo_Carga_TP1056.pin1
  N13: Sensor.2, Sensor.OUT, Pla_Cprincipal.A4, Foto_Celda.pin2
  N14: Pla_Cprincipal.A5, Modulo_Carga_TP1056.pin4, VCC1.+, 10K.Pin_1
  N15: Pla_Cprincipal.A6, Onderdeel3.HORZ
  N16: Pla_Cprincipal.A7, Onderdeel3.VERT
  N17: Pla_Cprincipal.D17_PWM/RX2, Bluetooth.TXD
  N18: Pla_Cprincipal.D16_PWM/TX2, Bluetooth.RXD
  N19: Pla_Cprincipal.VIN, Switch-_Encendido.leg1
  N20: Pla_Cprincipal.D2_PWM, Seguir_Al_Sol.1, R15.Pin_1
  N21: Pla_Cprincipal.D3_PWM, Un_solo_motor.1, R14.Pin_1
  N22: Pla_Cprincipal.D4_PWM, Modo_Manual.1, R13.Pin_1
  N23: Pla_Cprincipal.D7_PWM, Servo_Horizonal.pulse
  N24: Pla_Cprincipal.D50, SD_Card.MISO
  N25: Pla_Cprincipal.D51, SD_Card.MOSI
  N26: Pla_Cprincipal.D52, SD_Card.SCK
  N27: Pla_Cprincipal.D53, SD_Card.CS
  N28: Modulo_Carga_TP1056.pin3, Switch-_Encendido.leg0
  N29: Modulo_Carga_TP1056.pin5, VCC1.-
  N30: Onderdeel3.VCC, Seguir_Al_Sol.3, Un_solo_motor.3

custom parts:
  Tiny RTC: Tiny RTC I2C module DS1370Z RTC and AT24C32 EEPROM
  ACS712 Current Sensor 5A 20A 30A: Remix by Michael Kubina http://www.kubina.info Original by: https://forum.fritzing.org/t/current-sensor-5a-acs712/7694 https://forum.fritzing.org/u/ArtHome ArtHome12@gmail.com
  SD Card Module: SD Card Module Slot Socket Reader For Arduino ARM MCU
  TP4056: A DIP stand-in part for whatever IC you want. With 6 pins on a 300mil dual inline package (DIP) footprint.
  Bluetooth HC-06u: Bluetooth HC-06 - face up, pins down 16.5mm x 37.5mm PCB
